# Fritzing sketch Colour Word Clock PCBV08 (saved by Fritzing 0.9.3b)
circuit board: 9.00516cm x 5.59531cm

parts:
  R5 = Resistor [tolerance=±5% resistance=470 power=0.25 package=THT]
  1000_uF = Electrolytic Capacitor [capacitance=1mF voltage=16V package="100 mil [THT, electrolytic]"]
  Part2 = Arduino Nano (Rev3.0) (ICSP)
  Bluetooth = male pin header, 6 pins [form="♂ (male)"]
  RTCclock2 = female pin header, 6 pins [form="♀ (female)"]
  LDR = male pin header, 2 pins [form="♂ (male)"]
  R13 = Resistor [tolerance=±5% resistance=22k package=THT]
  RTC-clock = female pin header, 6 pins [form="♀ (female)"]
  RTCclock5 = female pin header, 6 pins [form="♀ (female)"]
  RTCclock6 = female pin header, 3 pins [form="♀ (female)"]
  RTCclock4 = female pin header, 3 pins [form="♀ (female)"]
  RTCclock3 = female pin header, 3 pins [form="♀ (female)"]
  RTCclock7 = female pin header, 2 pins [form="♀ (female)"]
  RTCclock8 = female pin header, 6 pins [form="♀ (female)"]
  R16 = Resistor [tolerance=±5% resistance=1.1k package=THT]
  R17 = Resistor [tolerance=±5% resistance=2.2k package=THT]
  RTCclock9 = female pin header, 6 pins [form="♀ (female)"]
  RTCclock10 = female pin header, 6 pins [form="♀ (female)"]
  Rotary = female pin header, 3 pins [form="♀ (female)"]
  DCF = female pin header, 3 pins [form="♀ (female)"]
  J1 = Screw terminal - 2 pins [package=THT]
  R18 = Resistor [tolerance=±5% resistance=470k package=THT]
  RTCclock11 = female pin header, 4 pins [form="♀ (female)"]
  R19 = Resistor [tolerance=±5% resistance=470k package=THT]
  - = LED - 3mm [color="Red (633nm)" package="3 mm [THT]"]
  -_2 = LED - 3mm [color="Yellow (592nm)" package="3 mm [THT]"]

nets:
  N1: R5.Pin_0, RTCclock6.pin1
  N2: R5.Pin_1, Part2.D5
  N3: 1000_uF.-, Part2.GND, Bluetooth.pin4, R13.Pin_0, RTC-clock.pin1, RTCclock5.pin6, RTCclock6.pin2, RTCclock3.pin1, RTCclock3.pin2, RTCclock3.pin3, RTCclock7.pin2, R17.Pin_1, DCF.pin3, J1.pin1
  N4: 1000_uF.+, Part2.5V, Bluetooth.pin5, LDR.pin2, RTC-clock.pin2, RTCclock5.pin4, RTCclock6.pin3, RTCclock4.pin1, RTCclock4.pin2, RTCclock4.pin3, RTCclock7.pin1, DCF.pin1, J1.pin2
  N5: Part2.D2, DCF.pin2
  N6: Part2.D3, Rotary.pin2
  N7: Part2.D4, Rotary.pin3
  N8: Part2.D6, R16.Pin_0
  N9: Part2.D7, Bluetooth.pin3, RTCclock5.pin3
  N10: Part2.D8, Rotary.pin1
  N11: Part2.D9, R19.Pin_0
  N12: Part2.D10, RTCclock11.pin3
  N13: Part2.D11/MOSI, RTCclock11.pin2
  N14: Part2.D12/MISO, RTCclock11.pin1
  N15: Part2.A5, RTC-clock.pin4
  N16: Part2.A4, RTC-clock.pin3
  N17: Part2.A2, LDR.pin1, R13.Pin_1
  N18: Part2.D13/SCK, R18.Pin_1
  N19: Bluetooth.pin2, RTCclock5.pin2, R16.Pin_1, R17.Pin_0
  N20: RTCclock2.pin1, RTCclock9.pin1
  N21: RTCclock2.pin2, RTCclock9.pin2
  N22: RTCclock2.pin3, RTCclock9.pin3
  N23: RTCclock2.pin4, RTCclock9.pin4
  N24: RTCclock2.pin5, RTCclock9.pin5
  N25: RTCclock2.pin6, RTCclock9.pin6
  N26: RTCclock8.pin1, RTCclock10.pin1
  N27: RTCclock8.pin2, RTCclock10.pin2
  N28: RTCclock8.pin3, RTCclock10.pin3
  N29: RTCclock8.pin4, RTCclock10.pin4
  N30: RTCclock8.pin5, RTCclock10.pin5
  N31: RTCclock8.pin6, RTCclock10.pin6
  N32: R18.Pin_0, -.anode
  N33: RTCclock11.pin4, R19.Pin_1, -_2.anode
  N34: -.cathode, -_2.cathode

notes:
  +
  -
  Gnd
  5V
  32K
  SQW
  SCL
  SDA
  State
  <-RX
  TX->
  EN
  Signal to LED
  Power
  TX
  RX
  Key
  3.3
  1A
  A5
  A4
  D5
  Signal
  DCF
  D8
  D3
  D4
  A3
  A2
